// Logisim project ALU.circ as structural Verilog
module ALU (
  input  [15:0] in_1,
  input  [15:0] in_2,
  input  [2:0] in_3,
  output [15:0] out_4
);

  wire [15:0] and_1_out, multiplier_1_out, nor_1_out, or_1_out, subtractor_1_out;

  assign and_1_out = in_1 & in_2;  // AND_Gate and_1, 16 bits wide
  assign nor_1_out = ~(in_1 | in_2);  // NOR_Gate nor_1, 16 bits wide
  assign or_1_out = in_1 | in_2;  // OR_Gate or_1, 16 bits wide
  Subtractor #(.width(16)) subtractor_1 (.a(in_1), .b(in_2), .out(subtractor_1_out));  // open: bin, bout
  Multiplier #(.width(16)) multiplier_1 (.a(in_1), .b(in_2), .out(multiplier_1_out));  // open: cin, cout
  Multiplexer #(.select(3), .width(16), .enable("false")) multiplexer_1 (
    .in0(and_1_out), .in1(nor_1_out), .in2(or_1_out), .in3(subtractor_1_out), .in4(multiplier_1_out),
    .out(out_4), .sel(in_3));  // open: in5, in6, in7
endmodule

module CPU (
);

  wire alu_1_p1, alu_1_p2;
  wire [19:0] rom_1_data;

  Register #(.width(16)) PC ();  // open: D, en, Q, clk, clr
  ROM #(.addrWidth(16), .dataWidth(20)) rom_1 (.data(rom_1_data));  // open: addr, sel
  // ALU alu_1: pin names not known; wires that end beside it: alu_1_p1, alu_1_p2, alu_1_p1, alu_1_p2
endmodule
